# Fritzing sketch TheMailboxChecker (saved by Fritzing 0.9.3b)
circuit board: 8.53488cm x 6cm

parts:
  Q3 = Basic FET P-Channel [part_number=FQP27P06 package="TO220 [THT]"]
  BAT1 = Battery block 9V
  REED1 = KY-021 Mini Magnetic Reed Switch Module [part_number=WPM308 package="Breakout board"]
  U1 = ESP32-38PinWide [part_number=ESP32-38PinWide]
  Q2 = Basic FET N-Channel [part_number=IRL540 package="TO220 [THT]"]
  Q1 = Basic FET N-Channel [part_number=IRLZ44 package="TO220 [THT]"]
  R1 = Resistor [tolerance=±5% resistance=10k package=THT]
  R2 = Resistor [tolerance=±5% resistance=10 package=THT]
  D1 = Rectifier Diode [part_number=1N4001 package="300 mil [THT]"]

nets (from the pcb view):
  N1: Q3.gate, Q2.drain, Q1.drain, R2.Pin_0
  N2: Q3.drain, U1.VIN
  N3: Q3.source, REED1.Vin, R2.Pin_1, D1.cathode
  N4: BAT1.-, REED1.-, U1.GND, Q2.source, Q1.source, R1.Pin_1
  N5: BAT1.+, D1.anode
  N6: REED1.S, Q1.gate, R1.Pin_0
  N7: U1.GPIO12, Q2.gate

notes:
  Antenne
  MD
  ESP1
  BAT1
  D1
  REED1
  Q1
  R1
  R2
  Q2
  Q3
  +
  -
  The Mailbox Checker

custom parts:
  KY-021 Mini Magnetic Reed Switch Module: KY-021 magnetic reed switch module. A reed switch is a magnetic sensor that is normally open and gets closed when exposed to a magnetic field.
  ESP32-38PinWide: Generic 38-Pin ESP32 with wide format (only access to one side of pins on a breadboard) based on Stephen Lilley's HiLetgo ESP-WROOM-32 ESP32 ESP-32S Development Board.
